# Fritzing sketch Dishwasher Microcontroller (saved by Fritzing 0.9.3b)
circuit board: 8.46667cm x 5.64444cm
breadboards: 2

parts:
  OnOff = Pushbutton [package="[THT]"]
  SP1 = Pushbutton [package="[THT]"]
  SP2 = Pushbutton [package="[THT]"]
  SP3 = Pushbutton [package="[THT]"]
  SP4 = Pushbutton [package="[THT]"]
  SP5 = Pushbutton [package="[THT]"]
  SP6 = Pushbutton [package="[THT]"]
  RP1 = Resistor [tolerance=±5% resistance=47k package=THT]
  RP2 = Resistor [tolerance=±5% resistance=22k package=THT]
  RP3 = Resistor [tolerance=±5% resistance=10k package=THT]
  RP5 = Resistor [tolerance=±5% resistance=2.2k package=THT]
  RP6 = Resistor [tolerance=±5% resistance=1k package=THT]
  RPR = Resistor [tolerance=±5% resistance=100k package=THT]
  U1 = 74HC595 [package="DIP16 [THT]"]
  Bauteil1 = Arduino Uno (Rev3)
  RP4 = Resistor [tolerance=±5% resistance=4.7k package=THT]
  R13 = Resistor [tolerance=±5% resistance=220 package=THT]
  R10 = Resistor [tolerance=±5% resistance=220 package=THT]
  R9 = Resistor [tolerance=±5% resistance=220 package=THT]
  R12 = Resistor [tolerance=±5% resistance=220 package=THT]
  R11 = Resistor [tolerance=±5% resistance=220 package=THT]
  R8 = Resistor [tolerance=±5% resistance=220 package=THT]
  LED1 = LED - 5mm [color="Red (633nm)" package="5 mm [THT]"]
  LED5 = LED - 5mm [color="Red (633nm)" package="5 mm [THT]"]
  LED3 = LED - 5mm [color="Red (633nm)" package="5 mm [THT]"]
  LED4 = LED - 5mm [color="Red (633nm)" package="5 mm [THT]"]
  LED2 = LED - 5mm [color="Red (633nm)" package="5 mm [THT]"]
  LED6 = LED - 5mm [color="Red (633nm)" package="5 mm [THT]"]
  StartReset = Pushbutton [package="[THT]"]
  Grove1 = Grove 4 Digit Display

nets:
  GND: OnOff.Pin_1, OnOff.Pin_2, RPR.Pin_1, U1.GND, U1.OE, Bauteil1.GND, LED1.anode, LED5.anode, LED3.anode, LED4.anode, LED2.anode, LED6.anode, StartReset.Pin_1, StartReset.Pin_2, Grove1.GND
  N1: OnOff.Pin_3, OnOff.Pin_4, Bauteil1.D4
  5V: SP1.Pin_1, SP1.Pin_2, SP2.Pin_1, SP2.Pin_2, SP3.Pin_1, SP3.Pin_2, SP4.Pin_1, SP4.Pin_2, SP5.Pin_1, SP5.Pin_2, SP6.Pin_1, SP6.Pin_2, RP1.Pin_1, RP2.Pin_1, RP3.Pin_1, RP5.Pin_1, RP6.Pin_1, RPR.Pin_0, U1.Q7', U1.Q0, Bauteil1.5V, RP4.Pin_1, Grove1.VCC
  N2: SP1.Pin_3, SP1.Pin_4, RP1.Pin_0, Bauteil1.A0
  N3: SP2.Pin_3, SP2.Pin_4, RP2.Pin_0
  N4: SP3.Pin_3, SP3.Pin_4, RP3.Pin_0
  N5: SP4.Pin_3, SP4.Pin_4, RP4.Pin_0
  N6: SP5.Pin_3, SP5.Pin_4, RP5.Pin_0
  N7: SP6.Pin_3, SP6.Pin_4, RP6.Pin_0
  N8: U1.Q2, R13.Pin_0
  N9: U1.Q3, R12.Pin_0
  N10: U1.Q4, R11.Pin_0
  N11: U1.Q5, R10.Pin_0
  N12: U1.Q6, R9.Pin_0
  N13: U1.Q7, R8.Pin_0
  N14: U1.SH_CP, Bauteil1.D13/SCK
  N15: U1.ST_CP, Bauteil1.D12/MISO
  N16: U1.DS, Bauteil1.D11_PWM/MOSI
  N17: Bauteil1.D3_PWM, Grove1.CLK
  N18: Bauteil1.D5_PWM, StartReset.Pin_3, StartReset.Pin_4
  N19: R13.Pin_1, LED6.cathode
  N20: R10.Pin_1, LED3.cathode
  N21: R9.Pin_1, LED2.cathode
  N22: R12.Pin_1, LED5.cathode
  N23: R11.Pin_1, LED4.cathode
  N24: R8.Pin_1, LED1.cathode
